# Fritzing sketch dogalgazalarm (saved by Fritzing 0.9.3b)
breadboards: 1

parts:
  Parça1 = Arduino Uno (Rev3)
  U1 = GAS_SENSOR [package=mq-3]
  J1 = Piezo Speaker
  R1 = Resistor [tolerance=±5% resistance=220 package=THT]

nets:
  N1: Parça1.A0, U1.A1
  N2: Parça1.D13/SCK, J1.pin2
  N3: Parça1.GND, R1.Pin_1
  N4: J1.pin1, R1.Pin_0
